// Logisim project ALU.circ as structural Verilog: 9 circuits, main circuit ALU
module ALU (
  input  [31:0] a,
  input  [31:0] b,
  input  [3:0] aluop,
  input  output_inverted,
  input  output_inc,
  input  clk,
  input  rst,
  output [31:0] res_low,
  output [31:0] res_high,
  output done
);

  wire divmulalu_1_done, not_1_out;
  wire [1:0] comparator_2_eq;
  wire [31:0] adder_1_out;
  wire [32:32] adder_1_cout;
  wire [63:0] adder_2_out, bit_extender_1_out, bit_extender_2_out, bit_extender_3_out,
       CombainationlALU_result_and, CombainationlALU_result_clo, CombainationlALU_result_clz,
       CombainationlALU_result_or, CombainationlALU_result_rotr, CombainationlALU_result_sra,
       CombainationlALU_result_srl, CombainationlALU_result_xor, CombainationlALU_resutl_sll,
       divmulalu_1_div_result, divmulalu_1_mul_result, multiplexer_1_out, multiplexer_2_out,
       multiplexer_3_out, not_2_out, not_3_out;

  not not_1 (not_1_out, rst);
  assign bit_extender_1_out = {{32{1'b0}}, b};  // Bit_Extender bit_extender_1
  DivMulALU divmulalu_1 (
    .a(a), .b(b), .clk(clk), .AluOp(aluop), .rst(not_1_out), .Div_result(divmulalu_1_div_result),
    .done(divmulalu_1_done), .Mul_result(divmulalu_1_mul_result));
  assign not_2_out = ~bit_extender_1_out;  // NOT_Gate not_2, 64 bits wide
  assign bit_extender_2_out = {{32{1'b0}}, a};  // Bit_Extender bit_extender_2
  Adder #(.width(32)) adder_1 (.a(a), .b(b), .out(adder_1_out), .cout(adder_1_cout[32]));  // open: cin
  Adder #(.width(64)) adder_2 (.a(bit_extender_2_out), .b(not_2_out), .out(adder_2_out), .cin(1'b1));  // open: cout
  alu_combinational CombainationlALU (
    .a(a), .b(b), .result_AND(CombainationlALU_result_and), .result_OR(CombainationlALU_result_or),
    .result_XOR(CombainationlALU_result_xor), .result_CLO(CombainationlALU_result_clo),
    .result_CLZ(CombainationlALU_result_clz), .resutl_SLL(CombainationlALU_resutl_sll),
    .result_SRL(CombainationlALU_result_srl), .result_SRA(CombainationlALU_result_sra),
    .result_ROTR(CombainationlALU_result_rotr));
  assign bit_extender_3_out = {{31{1'b0}}, {adder_1_cout[32], adder_1_out}};  // Bit_Extender bit_extender_3
  Multiplexer #(.select(4), .width(64)) multiplexer_1 (
    .in0(bit_extender_3_out), .in1(adder_2_out), .in2(divmulalu_1_mul_result), .in3(divmulalu_1_div_result),
    .in4(CombainationlALU_result_and), .in5(CombainationlALU_result_or), .in6(CombainationlALU_result_xor),
    .in7(CombainationlALU_result_clo), .in8(CombainationlALU_result_clz), .in9(CombainationlALU_resutl_sll),
    .in10(CombainationlALU_result_srl), .in11(CombainationlALU_result_sra),
    .in12(CombainationlALU_result_rotr), .out(multiplexer_1_out), .sel(aluop));  // open: in13, in14, in15
  assign not_3_out = ~multiplexer_1_out;  // NOT_Gate not_3, 64 bits wide
  Multiplexer #(.width(64)) multiplexer_2 (
    .in0(multiplexer_1_out), .in1(not_3_out), .out(multiplexer_2_out), .sel(output_inverted));
  Multiplexer #(.width(64)) multiplexer_3 (.in0({64{1'b0}}), .in1(64'h1), .out(multiplexer_3_out), .sel(output_inc));
  Comparator #(.width(4)) comparator_1 (.a(aluop), .b(4'b0010), .eq(comparator_2_eq[1]));  // open: gt, lt
  Comparator #(.width(4)) comparator_2 (.a(aluop), .b(4'b0011), .eq(comparator_2_eq[0]));  // open: gt, lt
  Adder #(.width(64)) adder_3 (
    .a(multiplexer_2_out), .b(multiplexer_3_out), .out({res_high, res_low}));  // open: cin, cout
  Multiplexer #(.select(2)) multiplexer_4 (
    .in0(1'b1), .in1(divmulalu_1_done), .in2(divmulalu_1_done), .out(done), .sel(comparator_2_eq));  // open: in3
endmodule

module alu_combinational (
  input  [31:0] a,
  input  [31:0] b,
  output [63:0] result_AND,
  output [63:0] result_OR,
  output [63:0] result_XOR,
  output [63:0] result_CLO,
  output [63:0] result_CLZ,
  output [63:0] resutl_SLL,
  output [63:0] result_SRL,
  output [63:0] result_SRA,
  output [63:0] result_ROTR
);

  wire [31:0] not_1_out;
  wire [63:0] bit_extender_1_out;

  assign not_1_out = ~a;  // NOT_Gate not_1, 32 bits wide
  assign bit_extender_1_out = {{32{a[31]}}, a};  // Bit_Extender bit_extender_1
  assign result_XOR[31:0] = b ^ a;  // XOR_Gate xor_1, 32 bits wide
  assign result_AND[31:0] = a & b;  // AND_Gate and_1, 32 bits wide
  assign result_OR[31:0] = a | b;  // OR_Gate or_1, 32 bits wide
  CLZ_circuit clz_circuit_1 (.a(not_1_out), .CLZ_out(result_CLO[5:0]));
  CLZ_circuit clz_circuit_2 (.a(a), .CLZ_out(result_CLZ[5:0]));
  Shifter_64Bit shifter_64bit_1 (
    .A({{32{1'b0}}, a}), .amount({1'b0, b[4:0]}), .dir(1'b0), .Shift_Type(1'b0), .Shifted_A(resutl_SLL));
  Shifter_64Bit shifter_64bit_2 (
    .A({{32{1'b0}}, a}), .amount({1'b0, b[4:0]}), .dir(1'b1), .Shift_Type(1'b0), .Shifted_A(result_SRL));
  Shifter_64Bit shifter_64bit_3 (
    .A(bit_extender_1_out), .amount({1'b0, b[4:0]}), .dir(1'b1), .Shift_Type(1'b1), .Shifted_A(result_SRA));
  Real_Rotator_32bit real_rotator_32bit_1 (.A(a), .amount(b[4:0]), .dir(1'b1), .Shifted_A(result_ROTR[31:0]));

  assign result_AND[63:32] = {32{1'b0}};
  assign result_CLO[63:6] = {58{1'b0}};
  assign result_CLZ[63:6] = {58{1'b0}};
  assign result_OR[63:32] = {32{1'b0}};
  assign result_ROTR[63:32] = {32{1'b0}};
  assign result_XOR[63:32] = {32{1'b0}};
endmodule

module CLZ_circuit (
  input  [31:0] a,
  output [5:0] CLZ_out
);

  wire [5:0] multiplexer_1_out, multiplexer_2_out, multiplexer_3_out, multiplexer_4_out, multiplexer_5_out,
       multiplexer_6_out, multiplexer_7_out, multiplexer_8_out, multiplexer_9_out, multiplexer_10_out,
       multiplexer_11_out, multiplexer_12_out, multiplexer_13_out, multiplexer_14_out, multiplexer_15_out,
       multiplexer_16_out, multiplexer_17_out, multiplexer_18_out, multiplexer_19_out, multiplexer_20_out,
       multiplexer_21_out, multiplexer_22_out, multiplexer_23_out, multiplexer_24_out, multiplexer_25_out,
       multiplexer_26_out, multiplexer_27_out, multiplexer_28_out, multiplexer_29_out, multiplexer_30_out,
       multiplexer_31_out;

  Multiplexer #(.width(6)) multiplexer_1 (.in0(6'b011111), .in1(6'b100000), .out(multiplexer_1_out), .sel(a[0]));
  Multiplexer #(.width(6)) multiplexer_2 (
    .in0(multiplexer_1_out), .in1(6'b011110), .out(multiplexer_2_out), .sel(a[1]));
  Multiplexer #(.width(6)) multiplexer_3 (
    .in0(multiplexer_2_out), .in1(6'b011101), .out(multiplexer_3_out), .sel(a[2]));
  Multiplexer #(.width(6)) multiplexer_4 (
    .in0(multiplexer_3_out), .in1(6'b011100), .out(multiplexer_4_out), .sel(a[3]));
  Multiplexer #(.width(6)) multiplexer_5 (
    .in0(multiplexer_4_out), .in1(6'b011011), .out(multiplexer_5_out), .sel(a[4]));
  Multiplexer #(.width(6)) multiplexer_6 (
    .in0(multiplexer_5_out), .in1(6'b011010), .out(multiplexer_6_out), .sel(a[5]));
  Multiplexer #(.width(6)) multiplexer_7 (
    .in0(multiplexer_6_out), .in1(6'b011001), .out(multiplexer_7_out), .sel(a[6]));
  Multiplexer #(.width(6)) multiplexer_8 (
    .in0(multiplexer_7_out), .in1(6'b011000), .out(multiplexer_8_out), .sel(a[7]));
  Multiplexer #(.width(6)) multiplexer_9 (
    .in0(multiplexer_8_out), .in1(6'b010111), .out(multiplexer_9_out), .sel(a[8]));
  Multiplexer #(.width(6)) multiplexer_10 (
    .in0(multiplexer_9_out), .in1(6'b010110), .out(multiplexer_10_out), .sel(a[9]));
  Multiplexer #(.width(6)) multiplexer_11 (
    .in0(multiplexer_10_out), .in1(6'b010101), .out(multiplexer_11_out), .sel(a[10]));
  Multiplexer #(.width(6)) multiplexer_12 (
    .in0(multiplexer_11_out), .in1(6'b010100), .out(multiplexer_12_out), .sel(a[11]));
  Multiplexer #(.width(6)) multiplexer_13 (
    .in0(multiplexer_12_out), .in1(6'b010011), .out(multiplexer_13_out), .sel(a[12]));
  Multiplexer #(.width(6)) multiplexer_14 (
    .in0(multiplexer_13_out), .in1(6'b010010), .out(multiplexer_14_out), .sel(a[13]));
  Multiplexer #(.width(6)) multiplexer_15 (
    .in0(multiplexer_14_out), .in1(6'b010001), .out(multiplexer_15_out), .sel(a[14]));
  Multiplexer #(.width(6)) multiplexer_16 (
    .in0(multiplexer_15_out), .in1(6'b010000), .out(multiplexer_16_out), .sel(a[15]));
  Multiplexer #(.width(6)) multiplexer_17 (
    .in0(multiplexer_16_out), .in1(6'b001111), .out(multiplexer_17_out), .sel(a[16]));
  Multiplexer #(.width(6)) multiplexer_18 (
    .in0(multiplexer_17_out), .in1(6'b001110), .out(multiplexer_18_out), .sel(a[17]));
  Multiplexer #(.width(6)) multiplexer_19 (
    .in0(multiplexer_18_out), .in1(6'b001101), .out(multiplexer_19_out), .sel(a[18]));
  Multiplexer #(.width(6)) multiplexer_20 (
    .in0(multiplexer_19_out), .in1(6'b001100), .out(multiplexer_20_out), .sel(a[19]));
  Multiplexer #(.width(6)) multiplexer_21 (
    .in0(multiplexer_20_out), .in1(6'b001011), .out(multiplexer_21_out), .sel(a[20]));
  Multiplexer #(.width(6)) multiplexer_22 (
    .in0(multiplexer_21_out), .in1(6'b001010), .out(multiplexer_22_out), .sel(a[21]));
  Multiplexer #(.width(6)) multiplexer_23 (
    .in0(multiplexer_22_out), .in1(6'b001001), .out(multiplexer_23_out), .sel(a[22]));
  Multiplexer #(.width(6)) multiplexer_24 (
    .in0(multiplexer_23_out), .in1(6'b001000), .out(multiplexer_24_out), .sel(a[23]));
  Multiplexer #(.width(6)) multiplexer_25 (
    .in0(multiplexer_24_out), .in1(6'b000111), .out(multiplexer_25_out), .sel(a[24]));
  Multiplexer #(.width(6)) multiplexer_26 (
    .in0(multiplexer_25_out), .in1(6'b000110), .out(multiplexer_26_out), .sel(a[25]));
  Multiplexer #(.width(6)) multiplexer_27 (
    .in0(multiplexer_26_out), .in1(6'b000101), .out(multiplexer_27_out), .sel(a[26]));
  Multiplexer #(.width(6)) multiplexer_28 (
    .in0(multiplexer_27_out), .in1(6'b000100), .out(multiplexer_28_out), .sel(a[27]));
  Multiplexer #(.width(6)) multiplexer_29 (
    .in0(multiplexer_28_out), .in1(6'b000011), .out(multiplexer_29_out), .sel(a[28]));
  Multiplexer #(.width(6)) multiplexer_30 (
    .in0(multiplexer_29_out), .in1(6'b000010), .out(multiplexer_30_out), .sel(a[29]));
  Multiplexer #(.width(6)) multiplexer_31 (
    .in0(multiplexer_30_out), .in1(6'b000001), .out(multiplexer_31_out), .sel(a[30]));
  Multiplexer #(.width(6)) multiplexer_32 (.in0(multiplexer_31_out), .in1({6{1'b0}}), .out(CLZ_out), .sel(a[31]));
endmodule

module Start_Signal_Handler (
  input  [31:0] a,
  input  clk,
  input  Mul_Div_Not,
  input  [3:0] AluOp,
  input  [31:0] b,
  output startSignal
);

  wire comparator_1_eq, comparator_2_eq, comparator_3_eq, not_1_out, not_2_out, or_1_out;
  wire [3:0] multiplexer_1_out;
  wire [31:0] aRegister_q, bRegister_q;

  Register #(.width(32)) aRegister (.D(a), .en(1'b1), .clk(clk), .Q(aRegister_q));  // open: clr
  Multiplexer #(.width(4)) multiplexer_1 (.in0(4'b0011), .in1(4'b0010), .out(multiplexer_1_out), .sel(Mul_Div_Not));
  Register #(.width(32)) bRegister (.D(b), .en(1'b1), .clk(clk), .Q(bRegister_q));  // open: clr
  Comparator #(.width(4)) comparator_1 (.a(multiplexer_1_out), .b(AluOp), .eq(comparator_1_eq));  // open: gt, lt
  Comparator #(.width(32)) comparator_2 (.a(aRegister_q), .b(a), .eq(comparator_2_eq));  // open: gt, lt
  Comparator #(.width(32)) comparator_3 (.a(bRegister_q), .b(b), .eq(comparator_3_eq));  // open: gt, lt
  not not_1 (not_1_out, comparator_2_eq);
  not not_2 (not_2_out, comparator_3_eq);
  or or_1 (or_1_out, not_1_out, not_2_out);
  and and_1 (startSignal, or_1_out, comparator_1_eq);
endmodule

module DivMulALU (
  input  [31:0] a,
  input  [31:0] b,
  input  clk,
  input  [3:0] AluOp,
  input  rst,
  output [63:0] Div_result,
  output done,
  output [63:0] Mul_result
);

  wire comparator_1_eq, divider32bit_1_done, multiplier32bit_1_done, start_signal_handler_1_startsignal,
       start_signal_handler_2_startsignal;

  Start_Signal_Handler start_signal_handler_1 (
    .a(a), .clk(clk), .Mul_Div_Not(1'b0), .AluOp(AluOp), .b(b),
    .startSignal(start_signal_handler_1_startsignal));
  Start_Signal_Handler start_signal_handler_2 (
    .a(a), .clk(clk), .Mul_Div_Not(1'b1), .AluOp(AluOp), .b(b),
    .startSignal(start_signal_handler_2_startsignal));
  Divider32Bit divider32bit_1 (
    .divisor(b), .dividend(a), .clk(clk), .start(start_signal_handler_1_startsignal),
    .quotient(Div_result[31:0]), .remainder(Div_result[63:32]), .done(divider32bit_1_done));
  Multiplier32Bit multiplier32bit_1 (
    .a(a), .b(b), .start(start_signal_handler_2_startsignal), .clk(clk), .rst_n(rst),
    .done(multiplier32bit_1_done), .res_lo(Mul_result[31:0]), .res_hi(Mul_result[63:32]));
  Comparator #(.width(4)) comparator_1 (.a(4'b0010), .b(AluOp), .eq(comparator_1_eq));  // open: gt, lt
  Multiplexer multiplexer_1 (
    .in0(divider32bit_1_done), .in1(multiplier32bit_1_done), .out(done), .sel(comparator_1_eq));
endmodule

module Real_Rotator_32bit (
  input  [31:0] A,
  input  [4:0] amount,
  input  dir,
  output [31:0] Shifted_A
);

  wire [31:0] left_rotator_1_data_out, multiplexer_1_out, reverse_32bit_1_shifted_a,
       reverse_32bit_2_shifted_a;

  Reverse_32bit reverse_32bit_1 (.A(A), .Shifted_A(reverse_32bit_1_shifted_a));
  Multiplexer #(.width(32)) multiplexer_1 (
    .in0(A), .in1(reverse_32bit_1_shifted_a), .out(multiplexer_1_out), .sel(dir));
  Left_Rotator left_rotator_1 (.Data_in(multiplexer_1_out), .shift_amount(amount), .Data_out(left_rotator_1_data_out));
  Reverse_32bit reverse_32bit_2 (.A(left_rotator_1_data_out), .Shifted_A(reverse_32bit_2_shifted_a));
  Multiplexer #(.width(32)) multiplexer_2 (
    .in0(left_rotator_1_data_out), .in1(reverse_32bit_2_shifted_a), .out(Shifted_A), .sel(dir));
endmodule

module Left_Rotator (
  input  [31:0] Data_in,
  input  [4:0] shift_amount,
  output [31:0] Data_out
);

  wire [31:0] multiplexer_1_out, multiplexer_2_out, multiplexer_3_out, multiplexer_4_out;

  Multiplexer #(.width(32)) multiplexer_1 (
    .in0(Data_in), .in1({Data_in[30:0], Data_in[31]}), .out(multiplexer_1_out), .sel(shift_amount[0]));
  Multiplexer #(.width(32)) multiplexer_2 (
    .in0(multiplexer_1_out), .in1({multiplexer_1_out[29:0], multiplexer_1_out[31:30]}),
    .out({multiplexer_2_out[3:0], multiplexer_2_out[31:4]}), .sel(shift_amount[1]));
  Multiplexer #(.width(32)) multiplexer_3 (
    .in0({multiplexer_2_out[3:0], multiplexer_2_out[31:4]}), .in1(multiplexer_2_out),
    .out(multiplexer_3_out), .sel(shift_amount[2]));
  Multiplexer #(.width(32)) multiplexer_4 (
    .in0(multiplexer_3_out), .in1({multiplexer_3_out[23:0], multiplexer_3_out[31:24]}),
    .out(multiplexer_4_out), .sel(shift_amount[3]));
  Multiplexer #(.width(32)) multiplexer_5 (
    .in0(multiplexer_4_out), .in1({multiplexer_4_out[15:0], multiplexer_4_out[31:16]}), .out(Data_out),
    .sel(shift_amount[4]));
endmodule

module Left_Shifter_64bit (
  input  [63:0] A,
  input  [5:0] Shift_amount,
  input  Fill_Bit,
  output [63:0] Data_out
);

  wire [1:0] bit_extender_1_out;
  wire [3:0] bit_extender_2_out, multiplexer_2_out;
  wire [7:0] bit_extender_3_out;
  wire [31:0] bit_extender_5_out, multiplexer_5_out, multiplexer_5_out_2;
  wire [59:0] multiplexer_2_out_2;
  wire [63:0] bit_extender_4_out, multiplexer_1_out, multiplexer_3_out;
  wire [63:48] multiplexer_4_out;

  assign bit_extender_1_out = {{1{Fill_Bit}}, Fill_Bit};  // Bit_Extender bit_extender_1
  assign bit_extender_2_out = {{3{Fill_Bit}}, Fill_Bit};  // Bit_Extender bit_extender_2
  assign bit_extender_3_out = {{7{Fill_Bit}}, Fill_Bit};  // Bit_Extender bit_extender_3
  assign bit_extender_4_out[15:0] = {{15{Fill_Bit}}, Fill_Bit};  // Bit_Extender bit_extender_4
  assign bit_extender_5_out = {{31{Fill_Bit}}, Fill_Bit};  // Bit_Extender bit_extender_5
  Multiplexer #(.width(64)) multiplexer_1 (
    .in0(A), .in1({A[62:0], Fill_Bit}), .out(multiplexer_1_out), .sel(Shift_amount[0]));
  Multiplexer #(.width(64)) multiplexer_2 (
    .in0(multiplexer_1_out), .in1({multiplexer_1_out[61:0], bit_extender_1_out}),
    .out({multiplexer_2_out, multiplexer_2_out_2}), .sel(Shift_amount[1]));
  Multiplexer #(.width(64)) multiplexer_3 (
    .in0({multiplexer_2_out, multiplexer_2_out_2}), .in1({multiplexer_2_out_2, bit_extender_2_out}),
    .out(multiplexer_3_out), .sel(Shift_amount[2]));
  Multiplexer #(.width(64)) multiplexer_4 (
    .in0(multiplexer_3_out), .in1({multiplexer_3_out[55:0], bit_extender_3_out}),
    .out({multiplexer_4_out, bit_extender_4_out[63:16]}), .sel(Shift_amount[3]));
  Multiplexer #(.width(64)) multiplexer_5 (
    .in0({multiplexer_4_out, bit_extender_4_out[63:16]}), .in1(bit_extender_4_out),
    .out({multiplexer_5_out, multiplexer_5_out_2}), .sel(Shift_amount[4]));
  Multiplexer #(.width(64)) multiplexer_6 (
    .in0({multiplexer_5_out, multiplexer_5_out_2}), .in1({multiplexer_5_out_2, bit_extender_5_out}),
    .out(Data_out), .sel(Shift_amount[5]));
endmodule

module Shifter_64Bit (
  input  [63:0] A,
  input  [5:0] amount,
  input  dir,
  input  Shift_Type,
  output [63:0] Shifted_A
);

  wire and_1_out;
  wire [63:0] left_shifter_64bit_1_data_out, multiplexer_1_out, reverse_1_shifted_a, reverse_2_shifted_a;

  and and_1 (and_1_out, A[63], Shift_Type, dir);
  Reverse reverse_1 (.A(A), .Shifted_A(reverse_1_shifted_a));
  Multiplexer #(.width(64)) multiplexer_1 (.in0(A), .in1(reverse_1_shifted_a), .out(multiplexer_1_out), .sel(dir));
  Left_Shifter_64bit left_shifter_64bit_1 (
    .A(multiplexer_1_out), .Shift_amount(amount), .Fill_Bit(and_1_out),
    .Data_out(left_shifter_64bit_1_data_out));
  Reverse reverse_2 (.A(left_shifter_64bit_1_data_out), .Shifted_A(reverse_2_shifted_a));
  Multiplexer #(.width(64)) multiplexer_2 (
    .in0(left_shifter_64bit_1_data_out), .in1(reverse_2_shifted_a), .out(Shifted_A), .sel(dir));
endmodule
