// Logisim project Divider.circ as structural Verilog: 1 circuit, main circuit Divider32Bit
module Divider32Bit (
  input  [31:0] divisor,
  input  [31:0] dividend,
  input  clk,
  input  start,
  output [31:0] quotient,
  output [31:0] remainder,
  output done
);

  wire comparator_1_eq, comparator_1_lt, not_1_out, or_1_out;
  wire [0:0] multiplexer_3_out;
  wire [4:0] counter_1_q;
  wire [31:0] divisorReg_q, multiplexer_1_out, multiplexer_2_out, multiplexer_4_out, subtractor_1_out;

  Register #(.width(32)) divisorReg (.D(divisor), .en(start), .clk(clk), .Q(divisorReg_q));  // open: clr
  Register #(.width(32)) dividenedReg (.D(multiplexer_1_out), .en(not_1_out), .clk(clk), .Q(quotient));  // open: clr
  Multiplexer #(.width(32)) multiplexer_1 (
    .in0({quotient[30:0], multiplexer_3_out[0]}), .in1(dividend), .out(multiplexer_1_out), .sel(start));
  Multiplexer #(.width(32)) multiplexer_2 (
    .in0(multiplexer_4_out), .in1({32{1'b0}}), .out(multiplexer_2_out), .sel(start));
  Counter #(.max('h3f), .ongoal("stay"), .width(6)) counter_1 (
    .clr(start), .up(1'b1), .count(1'b1), .clk(clk), .Q({done, counter_1_q}));  // open: load, D, carry
  Register #(.width(32)) RemainderReg (.D(multiplexer_2_out), .en(not_1_out), .clk(clk), .Q(remainder));  // open: clr
  Multiplexer multiplexer_3 (.in0(1'b0), .in1(1'b1), .out(multiplexer_3_out[0]), .sel(or_1_out));
  Comparator #(.mode("unsigned"), .width(32)) comparator_1 (
    .a(divisorReg_q), .b({remainder[30:0], quotient[31]}), .eq(comparator_1_eq), .lt(comparator_1_lt));  // open: gt
  Subtractor #(.width(32)) subtractor_1 (
    .a({remainder[30:0], quotient[31]}), .b(divisorReg_q), .out(subtractor_1_out));  // open: bin, bout
  not not_1 (not_1_out, done);
  or or_1 (or_1_out, comparator_1_eq, comparator_1_lt);
  Multiplexer #(.width(32)) multiplexer_4 (
    .in0({remainder[30:0], quotient[31]}), .in1(subtractor_1_out), .out(multiplexer_4_out), .sel(or_1_out));
endmodule
