// Logisim project MipsCPUPipeLined.circ as structural Verilog: 11 circuits, main circuit main
module main (
  input  clk,
  input  rst,
  input  Jen,
  input  [31:0] Jin,
  output [31:0] temp,
  output [31:0] Jout,
  output InstDone,
  output [31:0] R0,
  output [31:0] R1,
  output [31:0] R2,
  output [31:0] R3,
  output [31:0] R4,
  output [31:0] R5,
  output [31:0] R6,
  output [31:0] R7,
  output [31:0] R8,
  output [31:0] R9,
  output [31:0] R10,
  output [31:0] R11,
  output [31:0] R12,
  output [31:0] R13,
  output [31:0] R14,
  output [31:0] R15,
  output [31:0] R16,
  output [31:0] R17,
  output [31:0] R18,
  output [31:0] R19,
  output [31:0] R20,
  output [31:0] R21,
  output [31:0] R22,
  output [31:0] R23,
  output [31:0] R24,
  output [31:0] R25,
  output [31:0] R26,
  output [31:0] R27,
  output [31:0] R28,
  output [31:0] R29,
  output [31:0] R30,
  output [31:0] R31
);

  wire ALUSrc, and_1_out, and_2_out, and_3_out, and_5_out, and_6_out, Branch, comparator_1_eq, done, Jal,
       MemWrite, not_1_out, not_2_out, not_3_out, not_4_out, not_5_out, not_6_out, not_7_out, not_8_out,
       not_9_out, RegDst, RegWrite, ShiftInst, ShiftSRC, Stall, Stall2, Stall3, StallControl, ZeroSignal;
  wire [1:0] ALUOp, MemToReg, mfhi_mflo, PCSource;
  wire [3:0] ALUControlUnit_1_aluselector;
  wire [4:0] multiplexer_1_out, multiplexer_3_out, rd4, rs, rt4, rtRead, shamt;
  wire [5:0] funct, funct2, funct3, funct4, Opcode, Opcode2, Opcode3, Opcode4;
  wire [25:0] InstructionRegsiter1_jumpaddress;
  wire [31:0] adder_1_out, adder_2_out, ALU_1_res_high, ALU_1_res_low, ALUOut_q, ALUSrcB, and_7_out,
       bit_extender_1_out, bit_extender_2_out, BranchImmediate, DataMemoryJin, Hi,
       InstructionRegister3_instructionout, InstructionRegsiter1_instructionout, Lo, MipsMemory_1_dout,
       MipsMemory_2_dout, multiplexer_2_out, multiplexer_4_out, multiplexer_5_out, multiplexer_7_out,
       multiplexer_9_out, multiplexer_10_out, MuxOut, PC, register_1_q, RegisterFile_WriteData, RegOut1,
       RegOut1Branch, RegOut2, RegOut2Branch, SignExt_Immediate;

  Register #(.width(32)) u_PC (.D(multiplexer_4_out), .en(not_1_out), .clk(clk), .Q(PC), .clr(rst));
  not not_1 (not_1_out, Stall);
  ControlUnit ControlUnit_1 (
    .Opcode(Opcode), .funct(funct), .Opcode2(Opcode2), .funct2(funct2), .Opcode3(Opcode3), .funct3(funct3),
    .Opcode4(Opcode4), .funct4(funct4), .clk(clk), .rst(rst), .Stall(Stall), .RegDst(RegDst), .ALUop(ALUOp),
    .RegWrite(RegWrite), .MemToReg(MemToReg), .MemWrite(MemWrite), .ALUSrc(ALUSrc), .PCSource(PCSource),
    .Branch(Branch), .Jal(Jal), .shiftInst(ShiftInst), .shiftSRC(ShiftSRC), .StallControl(StallControl),
    .mfhi_mflo(mfhi_mflo), .Stall2(Stall2), .Stall3(Stall3));
  Register #(.width(32)) register_1 (.D(adder_1_out), .clk(clk), .Q(register_1_q), .clr(rst));  // open: en
  Adder #(.width(32)) adder_1 (.a(PC), .b(32'h1), .out(adder_1_out));  // open: cin, cout
  MipsMemory MipsMemory_1 (
    .Jen(Jen), .Wen(1'b0), .Jin(Jin), .Addr(PC[8:0]), .clk(clk), .Dout(MipsMemory_1_dout),
    .Jout(DataMemoryJin));  // open: Din
  Comparator #(.width(32)) comparator_1 (.a(RegOut1Branch), .b(RegOut2Branch), .eq(comparator_1_eq));  // open: gt, lt
  and and_1 (and_1_out, not_2_out, Branch);
  Adder #(.width(32)) adder_2 (.a(register_1_q), .b(BranchImmediate), .out(adder_2_out));  // open: cin, cout
  not not_2 (not_2_out, comparator_1_eq);
  Multiplexer #(.width(5)) multiplexer_1 (.in0(rt4), .in1(rd4), .out(multiplexer_1_out), .sel(RegDst));
  Multiplexer #(.width(32)) multiplexer_2 (
    .in0(adder_1_out), .in1(adder_2_out), .out(multiplexer_2_out), .sel(and_1_out));
  Multiplexer #(.width(5)) multiplexer_3 (.in0(multiplexer_1_out), .in1({5{1'b1}}), .out(multiplexer_3_out), .sel(Jal));
  IR_and_ID InstructionRegsiter1 (
    .Instruction(MipsMemory_1_dout), .Stall(Stall), .clk(clk), .rst(rst),
    .InstructionOut(InstructionRegsiter1_instructionout), .JumpAddress(InstructionRegsiter1_jumpaddress),
    .funct(funct), .shamt(shamt), .rt(rtRead), .rs(rs), .opcode(Opcode), .SignExt_Imd(BranchImmediate));  // open: rd
  and and_2 (and_2_out, not_3_out, RegWrite);
  not not_3 (not_3_out, Stall3);
  Multiplexer #(.select(2), .width(32)) multiplexer_4 (
    .in0(multiplexer_2_out), .in1({PC[31:26], InstructionRegsiter1_jumpaddress}), .in2(RegOut1Branch),
    .in3(RegOut1Branch), .out(multiplexer_4_out), .sel(PCSource));
  IR_and_ID InstructionRegsiter2 (
    .Instruction(InstructionRegsiter1_instructionout), .Stall(Stall), .clk(clk), .rst(rst),
    .InstructionOut(temp), .funct(funct2), .opcode(Opcode2), .SignExt_Imd(SignExt_Immediate));  // open: JumpAddress, shamt, rd, rt, rs
  RegisterFile RegisterFile_1 (
    .Read0(rs), .Read1(rtRead), .Write(multiplexer_3_out), .Data(RegisterFile_WriteData),
    .WriteReg(and_2_out), .clk(clk), .rst(rst), .RegOut1(RegOut1Branch), .RegOut2(RegOut2Branch), .Reg0(R0),
    .Reg1(R1), .Reg2(R2), .Reg3(R3), .Reg4(R4), .Reg5(R5), .Reg6(R6), .Reg7(R7), .Reg8(R8), .Reg9(R9),
    .Reg10(R10), .Reg11(R11), .Reg12(R12), .Reg13(R13), .Reg14(R14), .Reg15(R15), .Reg16(R16), .Reg17(R17),
    .Reg18(R18), .Reg19(R19), .Reg20(R20), .Reg21(R21), .Reg22(R22), .Reg23(R23), .Reg24(R24), .Reg25(R25),
    .Reg26(R26), .Reg27(R27), .Reg28(R28), .Reg29(R29), .Reg30(R30), .Reg31(R31));
  Register #(.width(32)) ReadData2 (.D(RegOut2Branch), .en(not_4_out), .clk(clk), .Q(RegOut2), .clr(rst));
  not not_4 (not_4_out, Stall);
  Register #(.width(32)) ReadData1 (.D(RegOut1Branch), .en(not_5_out), .clk(clk), .Q(RegOut1), .clr(rst));
  not not_5 (not_5_out, Stall);
  assign bit_extender_1_out = {{27{1'b0}}, shamt};  // Bit_Extender bit_extender_1
  Multiplexer #(.width(32)) multiplexer_5 (.in0(RegOut1), .in1(RegOut2), .out(multiplexer_5_out), .sel(and_3_out));
  Multiplexer #(.width(32)) multiplexer_6 (.in0(SignExt_Immediate), .in1(RegOut2), .out(MuxOut), .sel(ALUSrc));
  ALUControlUnit ALUControlUnit_1 (.funct(funct2), .ALUOp(ALUOp), .ALUSelector(ALUControlUnit_1_aluselector));
  Multiplexer #(.width(32)) multiplexer_7 (
    .in0(bit_extender_1_out), .in1(RegOut2), .out(multiplexer_7_out), .sel(ShiftSRC));
  and and_3 (and_3_out, ShiftInst, not_6_out);
  Multiplexer #(.width(32)) multiplexer_8 (.in0(MuxOut), .in1(multiplexer_7_out), .out(ALUSrcB), .sel(ShiftInst));
  not not_6 (not_6_out, ShiftSRC);
  ALU ALU_1 (
    .a(multiplexer_5_out), .b(ALUSrcB), .aluop(ALUControlUnit_1_aluselector), .output_inverted(1'b0),
    .output_inc(1'b0), .clk(clk), .rst(rst), .res_low(ALU_1_res_low), .res_high(ALU_1_res_high), .done(done));
  not not_7 (not_7_out, done);
  and and_4 (Stall, StallControl, not_7_out);
  Register #(.width(32)) u_Lo (.D(ALU_1_res_low), .en(StallControl), .clk(clk), .Q(Lo), .clr(rst));
  Register #(.width(32)) ALUOut (.D(ALU_1_res_low), .clk(clk), .Q(ALUOut_q), .clr(rst));  // open: en
  Register #(.width(32)) u_Hi (.D(ALU_1_res_high), .en(StallControl), .clk(clk), .Q(Hi), .clr(rst));
  IR_and_ID InstructionRegister3 (
    .Instruction(temp), .Stall(Stall2), .clk(clk), .rst(rst),
    .InstructionOut(InstructionRegister3_instructionout), .funct(funct3), .opcode(Opcode3));  // open: JumpAddress, shamt, rd, rt, rs, SignExt_Imd
  Comparator #(.width(32)) comparator_2 (.a(ALU_1_res_low), .b({32{1'b0}}), .eq(ZeroSignal));  // open: gt, lt
  and and_5 (and_5_out, MemWrite, not_8_out);
  not not_8 (not_8_out, Stall2);
  not not_9 (not_9_out, ZeroSignal);
  and and_6 (and_6_out, ALUOut_q[31], not_9_out);
  MipsMemory MipsMemory_2 (
    .Jen(Jen), .Wen(and_5_out), .Din(RegOut2), .Jin(DataMemoryJin), .Addr(ALUOut_q[8:0]), .clk(clk),
    .Dout(MipsMemory_2_dout), .Jout(Jout));
  assign bit_extender_2_out = {{31{1'b0}}, and_6_out};  // Bit_Extender bit_extender_2
  assign and_7_out = PC & 32'h1ff;  // AND_Gate and_7, 32 bits wide
  Multiplexer #(.select(2), .width(32)) multiplexer_9 (
    .in0(MipsMemory_2_dout), .in1(ALUOut_q), .in2(and_7_out), .in3(bit_extender_2_out),
    .out(multiplexer_9_out), .sel(MemToReg));
  IR_and_ID InstructionRegsiter4 (
    .Instruction(InstructionRegister3_instructionout), .Stall(Stall3), .clk(clk), .rst(rst), .funct(funct4),
    .rd(rd4), .rt(rt4), .opcode(Opcode4));  // open: InstructionOut, JumpAddress, shamt, rs, SignExt_Imd
  Register #(.width(32)) register_2 (
    .D(multiplexer_10_out), .clk(clk), .Q(RegisterFile_WriteData), .clr(rst));  // open: en
  Multiplexer #(.select(2), .width(32)) multiplexer_10 (
    .in0(multiplexer_9_out), .in1(Lo), .in2(Hi), .in3(Hi), .out(multiplexer_10_out), .sel(mfhi_mflo));
  InstDoneCircuit InstDoneCircuit_1 (.Stall3(Stall3), .clk(clk), .rst(rst), .InstDone(InstDone));

  // Other names for the same wires on the sheet: InstructionOut2[31:0] = temp
endmodule

module ALUControlUnit (
  input  [5:0] funct,
  input  [1:0] ALUOp,
  output [3:0] ALUSelector
);

  ROM #(.dataWidth(4)) HelperROM (.addr({ALUOp, funct}), .data(ALUSelector));

  // Notes on the sheet:
  //   contents of HelperROM (hex, n*v repeats v):
  //   64*0 64*1 9 0 0 0 9 0 a b 18*0 3 7*0 1 0 4 5 6
endmodule

module ALUDecoder (
  input  O5,
  input  O4,
  input  O3,
  input  O2,
  input  O1,
  input  O0,
  output ALUOP1,
  output ALUOP0
);

  wire and_2_out, and_3_out, not_1_out, not_2_out, not_3_out, not_4_out, not_5_out, not_6_out;

  not not_1 (not_1_out, O5);
  not not_2 (not_2_out, O4);
  not not_3 (not_3_out, O3);
  not not_4 (not_4_out, O2);
  not not_5 (not_5_out, O1);
  not not_6 (not_6_out, O0);
  and and_1 (ALUOP1, not_2_out, not_3_out, not_4_out, not_5_out, not_6_out);
  and and_2 (and_2_out, not_1_out, not_2_out, not_3_out, O2, not_5_out, O0);
  and and_3 (and_3_out, not_1_out, not_2_out, O3, not_4_out, O1, not_6_out);
  or or_1 (ALUOP0, and_2_out, and_3_out);
endmodule

module ControlUnit (
  input  [5:0] Opcode,
  input  [5:0] funct,
  input  [5:0] Opcode2,
  input  [5:0] funct2,
  input  [5:0] Opcode3,
  input  [5:0] funct3,
  input  [5:0] Opcode4,
  input  [5:0] funct4,
  input  clk,
  input  rst,
  input  Stall,
  output RegDst,
  output [1:0] ALUop,
  output RegWrite,
  output [1:0] MemToReg,
  output MemWrite,
  output ALUSrc,
  output [1:0] PCSource,
  output Branch,
  output Jal,
  output shiftInst,
  output shiftSRC,
  output StallControl,
  output [1:0] mfhi_mflo,
  output Stall2,
  output Stall3
);

  wire and_1_out, comparator_2_eq, comparator_3_eq, comparator_4_eq, comparator_5_eq, comparator_6_eq,
       comparator_7_eq, comparator_8_eq, comparator_9_eq, comparator_10_eq, comparator_12_eq,
       comparator_13_eq, comparator_14_eq, comparator_15_eq, comparator_16_eq, comparator_19_eq,
       comparator_21_eq, comparator_22_eq, comparator_23_eq, comparator_24_eq, comparator_25_eq,
       comparator_26_eq, not_1_out, or_4_out;

  Comparator #(.width(6)) comparator_1 (.a(Opcode4), .b({6{1'b0}}), .eq(RegDst));  // open: gt, lt
  not not_1 (not_1_out, comparator_2_eq);
  Comparator #(.width(6)) comparator_2 (.a(funct4), .b({6{1'b0}}), .eq(comparator_2_eq));  // open: gt, lt
  Comparator #(.width(6)) comparator_3 (.a(Opcode4), .b({6{1'b0}}), .eq(comparator_3_eq));  // open: gt, lt
  Comparator #(.width(6)) comparator_4 (.a(Opcode4), .b(6'b000011), .eq(comparator_4_eq));  // open: gt, lt
  Comparator #(.width(6)) comparator_5 (.a(Opcode4), .b(6'b100011), .eq(comparator_5_eq));  // open: gt, lt
  Comparator #(.width(6)) comparator_6 (.a(Opcode4), .b(6'b001000), .eq(comparator_6_eq));  // open: gt, lt
  Comparator #(.width(6)) comparator_7 (.a(Opcode4), .b(6'b001010), .eq(comparator_7_eq));  // open: gt, lt
  Comparator #(.width(6)) comparator_8 (.a(Opcode3), .b({6{1'b0}}), .eq(comparator_8_eq));  // open: gt, lt
  Comparator #(.width(6)) comparator_9 (.a(Opcode3), .b(6'b001010), .eq(comparator_9_eq));  // open: gt, lt
  Comparator #(.width(6)) comparator_10 (.a(Opcode3), .b(6'b000011), .eq(comparator_10_eq));  // open: gt, lt
  Comparator #(.width(6)) comparator_11 (.a(Opcode3), .b(6'b101011), .eq(MemWrite));  // open: gt, lt
  Comparator #(.width(6)) comparator_12 (.a(Opcode2), .b(6'b000101), .eq(comparator_12_eq));  // open: gt, lt
  Comparator #(.width(6)) comparator_13 (.a(Opcode), .b(6'b000011), .eq(comparator_13_eq));  // open: gt, lt
  Comparator #(.width(6)) comparator_14 (.a(Opcode), .b(6'b000010), .eq(comparator_14_eq));  // open: gt, lt
  Comparator #(.width(6)) comparator_15 (.a(funct), .b(6'b001000), .eq(comparator_15_eq));  // open: gt, lt
  Comparator #(.width(6)) comparator_16 (.a(Opcode), .b({6{1'b0}}), .eq(comparator_16_eq));  // open: gt, lt
  Comparator #(.width(6)) comparator_17 (.a(Opcode), .b(6'b000101), .eq(Branch));  // open: gt, lt
  Comparator #(.width(6)) comparator_18 (.a(Opcode4), .b(6'b000011), .eq(Jal));  // open: gt, lt
  Comparator #(.width(6)) comparator_19 (.a(Opcode2), .b({6{1'b0}}), .eq(comparator_19_eq));  // open: gt, lt
  and and_1 (and_1_out, not_1_out, comparator_3_eq);
  or or_1 (RegWrite, and_1_out, comparator_4_eq, comparator_5_eq, comparator_6_eq, comparator_7_eq);
  or or_2 (PCSource[0], comparator_13_eq, comparator_14_eq);
  and and_2 (PCSource[1], comparator_15_eq, comparator_16_eq);
  Comparator #(.width(6)) comparator_20 (.a(funct2), .b(6'b000100), .eq(shiftSRC));  // open: gt, lt
  Comparator #(.width(6)) comparator_21 (.a(funct2), .b({6{1'b0}}), .eq(comparator_21_eq));  // open: gt, lt
  Comparator #(.width(6)) comparator_22 (.a(funct3), .b(6'b010010), .eq(comparator_22_eq));  // open: gt, lt
  Comparator #(.width(6)) comparator_23 (.a(Opcode3), .b({6{1'b0}}), .eq(comparator_23_eq));  // open: gt, lt
  Comparator #(.width(6)) comparator_24 (.a(funct3), .b(6'b010000), .eq(comparator_24_eq));  // open: gt, lt
  ALUDecoder ALUDecoder_1 (
    .O5(Opcode2[5]), .O4(Opcode2[4]), .O3(Opcode2[3]), .O2(Opcode2[2]), .O1(Opcode2[1]), .O0(Opcode2[0]),
    .ALUOP1(ALUop[1]), .ALUOP0(ALUop[0]));
  Comparator #(.width(6)) comparator_25 (.a(Opcode3), .b(6'b001000), .eq(comparator_25_eq));  // open: gt, lt
  or or_3 (ALUSrc, comparator_19_eq, comparator_12_eq);
  or or_4 (or_4_out, shiftSRC, comparator_21_eq);
  Comparator #(.width(6)) comparator_26 (.a(funct2), .b(6'b011010), .eq(comparator_26_eq));  // open: gt, lt
  or or_5 (MemToReg[0], comparator_8_eq, comparator_9_eq, comparator_25_eq);
  or or_6 (MemToReg[1], comparator_9_eq, comparator_10_eq);
  and and_3 (shiftInst, or_4_out, comparator_19_eq);
  and and_4 (StallControl, comparator_19_eq, comparator_26_eq);
  and and_5 (mfhi_mflo[0], comparator_22_eq, comparator_23_eq);
  and and_6 (mfhi_mflo[1], comparator_23_eq, comparator_24_eq);
  D_Flip_Flop d_ff_1 (.D(Stall), .clk(clk), .Q(Stall2), .reset(rst));  // open: Qn, preset
  D_Flip_Flop d_ff_2 (.D(Stall2), .clk(clk), .Q(Stall3), .reset(rst));  // open: Qn, preset

  // Other names for the same wires on the sheet: jr = PCSource[1]
endmodule

module RegisterFile (
  input  [4:0] Read0,
  input  [4:0] Read1,
  input  [4:0] Write,
  input  [31:0] Data,
  input  WriteReg,
  input  clk,
  input  rst,
  output [31:0] RegOut1,
  output [31:0] RegOut2,
  output [31:0] Reg0,
  output [31:0] Reg1,
  output [31:0] Reg2,
  output [31:0] Reg3,
  output [31:0] Reg4,
  output [31:0] Reg5,
  output [31:0] Reg6,
  output [31:0] Reg7,
  output [31:0] Reg8,
  output [31:0] Reg9,
  output [31:0] Reg10,
  output [31:0] Reg11,
  output [31:0] Reg12,
  output [31:0] Reg13,
  output [31:0] Reg14,
  output [31:0] Reg15,
  output [31:0] Reg16,
  output [31:0] Reg17,
  output [31:0] Reg18,
  output [31:0] Reg19,
  output [31:0] Reg20,
  output [31:0] Reg21,
  output [31:0] Reg22,
  output [31:0] Reg23,
  output [31:0] Reg24,
  output [31:0] Reg25,
  output [31:0] Reg26,
  output [31:0] Reg27,
  output [31:0] Reg28,
  output [31:0] Reg29,
  output [31:0] Reg30,
  output [31:0] Reg31
);

  wire decoder_1_out0, decoder_1_out1, decoder_1_out2, decoder_1_out3, decoder_1_out4, decoder_1_out5,
       decoder_1_out6, decoder_1_out7;
  wire [31:0] RegOut1_1, RegOut1_2, RegOut1_3, RegOut1_4, RegOut1_5, RegOut1_6, RegOut1_7, RegOut1_8,
       RegOut2_1, RegOut2_2, RegOut2_3, RegOut2_4, RegOut2_5, RegOut2_6, RegOut2_7, RegOut2_8;

  Decoder #(.select(3)) decoder_1 (
    .out0(decoder_1_out0), .out1(decoder_1_out1), .out2(decoder_1_out2), .out3(decoder_1_out3),
    .out4(decoder_1_out4), .out5(decoder_1_out5), .out6(decoder_1_out6), .out7(decoder_1_out7),
    .sel(Write[4:2]), .en(WriteReg));
  SubRegisterFile SubRegister000 (
    .isFirstRow(1'b1), .Read0(Read0[1:0]), .Read1(Read1[1:0]), .Write(Write[1:0]), .Data(Data),
    .WriteReg(decoder_1_out0), .clk(clk), .rst(rst), .RegOut1(RegOut1_1), .RegOut2(RegOut2_1), .Reg00(Reg0),
    .Reg01(Reg1), .Reg10(Reg2), .Reg11(Reg3));
  SubRegisterFile SubRegister001 (
    .isFirstRow(1'b0), .Read0(Read0[1:0]), .Read1(Read1[1:0]), .Write(Write[1:0]), .Data(Data),
    .WriteReg(decoder_1_out1), .clk(clk), .rst(rst), .RegOut1(RegOut1_2), .RegOut2(RegOut2_2), .Reg00(Reg4),
    .Reg01(Reg5), .Reg10(Reg6), .Reg11(Reg7));
  SubRegisterFile SubRegister010 (
    .isFirstRow(1'b0), .Read0(Read0[1:0]), .Read1(Read1[1:0]), .Write(Write[1:0]), .Data(Data),
    .WriteReg(decoder_1_out2), .clk(clk), .rst(rst), .RegOut1(RegOut1_3), .RegOut2(RegOut2_3), .Reg00(Reg8),
    .Reg01(Reg9), .Reg10(Reg10), .Reg11(Reg11));
  SubRegisterFile SubRegister011 (
    .isFirstRow(1'b0), .Read0(Read0[1:0]), .Read1(Read1[1:0]), .Write(Write[1:0]), .Data(Data),
    .WriteReg(decoder_1_out3), .clk(clk), .rst(rst), .RegOut1(RegOut1_4), .RegOut2(RegOut2_4), .Reg00(Reg12),
    .Reg01(Reg13), .Reg10(Reg14), .Reg11(Reg15));
  SubRegisterFile SubRegister100 (
    .isFirstRow(1'b0), .Read0(Read0[1:0]), .Read1(Read1[1:0]), .Write(Write[1:0]), .Data(Data),
    .WriteReg(decoder_1_out4), .clk(clk), .rst(rst), .RegOut1(RegOut1_5), .RegOut2(RegOut2_5), .Reg00(Reg16),
    .Reg01(Reg17), .Reg10(Reg18), .Reg11(Reg19));
  SubRegisterFile SubRegister101 (
    .isFirstRow(1'b0), .Read0(Read0[1:0]), .Read1(Read1[1:0]), .Write(Write[1:0]), .Data(Data),
    .WriteReg(decoder_1_out5), .clk(clk), .rst(rst), .RegOut1(RegOut1_6), .RegOut2(RegOut2_6), .Reg00(Reg20),
    .Reg01(Reg21), .Reg10(Reg22), .Reg11(Reg23));
  SubRegisterFile SubRegister110 (
    .isFirstRow(1'b0), .Read0(Read0[1:0]), .Read1(Read1[1:0]), .Write(Write[1:0]), .Data(Data),
    .WriteReg(decoder_1_out6), .clk(clk), .rst(rst), .RegOut1(RegOut1_7), .RegOut2(RegOut2_7), .Reg00(Reg24),
    .Reg01(Reg25), .Reg10(Reg26), .Reg11(Reg27));
  SubRegisterFile SubRegister111 (
    .isFirstRow(1'b0), .Read0(Read0[1:0]), .Read1(Read1[1:0]), .Write(Write[1:0]), .Data(Data),
    .WriteReg(decoder_1_out7), .clk(clk), .rst(rst), .RegOut1(RegOut1_8), .RegOut2(RegOut2_8), .Reg00(Reg28),
    .Reg01(Reg29), .Reg10(Reg30), .Reg11(Reg31));
  Multiplexer #(.select(3), .width(32)) multiplexer_1 (
    .in0(RegOut1_1), .in1(RegOut1_2), .in2(RegOut1_3), .in3(RegOut1_4), .in4(RegOut1_5), .in5(RegOut1_6),
    .in6(RegOut1_7), .in7(RegOut1_8), .out(RegOut1), .sel(Read0[4:2]));
  Multiplexer #(.select(3), .width(32)) multiplexer_2 (
    .in0(RegOut2_1), .in1(RegOut2_2), .in2(RegOut2_3), .in3(RegOut2_4), .in4(RegOut2_5), .in5(RegOut2_6),
    .in6(RegOut2_7), .in7(RegOut2_8), .out(RegOut2), .sel(Read1[4:2]));

  // Other names for the same wires on the sheet: Read0_t[1:0] = Read0[1:0]; Read0Select[2:0] = Read0[4:2];
  //   Read1_t[1:0] = Read1[1:0]; Read1Select[2:0] = Read1[4:2]; Write_t[1:0] = Write[1:0];
  //   WriteSelect[2:0] = Write[4:2]
endmodule

module SubRegisterFile (
  input  isFirstRow,
  input  [1:0] Read0,
  input  [1:0] Read1,
  input  [1:0] Write,
  input  [31:0] Data,
  input  WriteReg,
  input  clk,
  input  rst,
  output [31:0] RegOut1,
  output [31:0] RegOut2,
  output [31:0] Reg00,
  output [31:0] Reg01,
  output [31:0] Reg10,
  output [31:0] Reg11
);

  wire decoder_1_out0, decoder_1_out1, decoder_1_out2, decoder_1_out3;
  wire [31:0] multiplexer_1_out;

  Decoder #(.select(2)) decoder_1 (
    .out0(decoder_1_out0), .out1(decoder_1_out1), .out2(decoder_1_out2), .out3(decoder_1_out3), .sel(Write),
    .en(WriteReg));
  Multiplexer #(.width(32)) multiplexer_1 (.in0(Data), .in1({32{1'b0}}), .out(multiplexer_1_out), .sel(isFirstRow));
  Register #(.width(32)) R00 (.D(multiplexer_1_out), .en(decoder_1_out0), .clk(clk), .Q(Reg00), .clr(rst));
  Register #(.width(32)) R01 (.D(Data), .en(decoder_1_out1), .clk(clk), .Q(Reg01), .clr(rst));
  Register #(.width(32)) R10 (.D(Data), .en(decoder_1_out2), .clk(clk), .Q(Reg10), .clr(rst));
  Register #(.width(32)) R11 (.D(Data), .en(decoder_1_out3), .clk(clk), .Q(Reg11), .clr(rst));
  Multiplexer #(.select(2), .width(32)) multiplexer_2 (
    .in0(Reg00), .in1(Reg01), .in2(Reg10), .in3(Reg11), .out(RegOut1), .sel(Read0));
  Multiplexer #(.select(2), .width(32)) multiplexer_3 (
    .in0(Reg00), .in1(Reg01), .in2(Reg10), .in3(Reg11), .out(RegOut2), .sel(Read1));
endmodule

module SubMemoryLevel2 (
  input  Jen,
  input  Wen,
  input  [31:0] Din,
  input  [31:0] Jin,
  input  [2:0] Addr,
  input  clk,
  output [31:0] Dout,
  output [31:0] Jout
);

  wire Decoder000, Decoder001, Decoder010, Decoder011, Decoder100, Decoder101, Decoder110, Decoder111,
       or_1_out, or_2_out, or_3_out, or_4_out, or_5_out, or_6_out, or_7_out, or_8_out;
  wire [31:0] multiplexer_1_out, multiplexer_2_out, multiplexer_3_out, multiplexer_4_out, multiplexer_5_out,
       multiplexer_6_out, multiplexer_7_out, multiplexer_8_out, R00_q, R01_q, R10_q, R11_q, register_1_q,
       register_2_q, register_3_q;

  Decoder #(.select(3)) decoder_1 (
    .out0(Decoder000), .out1(Decoder001), .out2(Decoder010), .out3(Decoder011), .out4(Decoder100),
    .out5(Decoder101), .out6(Decoder110), .out7(Decoder111), .sel(Addr), .en(Wen));
  Multiplexer #(.width(32)) multiplexer_1 (.in0(Din), .in1(Jin), .out(multiplexer_1_out), .sel(Jen));
  Multiplexer #(.width(32)) multiplexer_2 (.in0(Din), .in1(R00_q), .out(multiplexer_2_out), .sel(Jen));
  Multiplexer #(.width(32)) multiplexer_3 (.in0(Din), .in1(R01_q), .out(multiplexer_3_out), .sel(Jen));
  Multiplexer #(.width(32)) multiplexer_4 (.in0(Din), .in1(R10_q), .out(multiplexer_4_out), .sel(Jen));
  or or_1 (or_1_out, Jen, Decoder000);
  or or_2 (or_2_out, Jen, Decoder001);
  or or_3 (or_3_out, Jen, Decoder010);
  or or_4 (or_4_out, Jen, Decoder011);
  Register #(.width(32)) R00 (.D(multiplexer_1_out), .en(or_1_out), .clk(clk), .Q(R00_q));  // open: clr
  Register #(.width(32)) R01 (.D(multiplexer_2_out), .en(or_2_out), .clk(clk), .Q(R01_q));  // open: clr
  Register #(.width(32)) R10 (.D(multiplexer_3_out), .en(or_3_out), .clk(clk), .Q(R10_q));  // open: clr
  Register #(.width(32)) R11 (.D(multiplexer_4_out), .en(or_4_out), .clk(clk), .Q(R11_q));  // open: clr
  Multiplexer #(.width(32)) multiplexer_5 (.in0(Din), .in1(R11_q), .out(multiplexer_5_out), .sel(Jen));
  Multiplexer #(.width(32)) multiplexer_6 (.in0(Din), .in1(register_1_q), .out(multiplexer_6_out), .sel(Jen));
  Multiplexer #(.width(32)) multiplexer_7 (.in0(Din), .in1(register_2_q), .out(multiplexer_7_out), .sel(Jen));
  Multiplexer #(.width(32)) multiplexer_8 (.in0(Din), .in1(register_3_q), .out(multiplexer_8_out), .sel(Jen));
  or or_5 (or_5_out, Jen, Decoder100);
  or or_6 (or_6_out, Jen, Decoder101);
  or or_7 (or_7_out, Jen, Decoder110);
  or or_8 (or_8_out, Jen, Decoder111);
  Register #(.width(32)) register_1 (.D(multiplexer_5_out), .en(or_5_out), .clk(clk), .Q(register_1_q));  // open: clr
  Register #(.width(32)) register_2 (.D(multiplexer_6_out), .en(or_6_out), .clk(clk), .Q(register_2_q));  // open: clr
  Register #(.width(32)) register_3 (.D(multiplexer_7_out), .en(or_7_out), .clk(clk), .Q(register_3_q));  // open: clr
  Register #(.width(32)) register_4 (.D(multiplexer_8_out), .en(or_8_out), .clk(clk), .Q(Jout));  // open: clr
  Multiplexer #(.select(3), .width(32)) multiplexer_9 (
    .in0(R00_q), .in1(R01_q), .in2(R10_q), .in3(R11_q), .in4(register_1_q), .in5(register_2_q),
    .in6(register_3_q), .in7(Jout), .out(Dout), .sel(Addr));
endmodule

module SubMemoryLevel1 (
  input  Jen,
  input  Wen,
  input  [31:0] Din,
  input  [31:0] Jin,
  input  [5:0] Addr,
  input  clk,
  output [31:0] Dout,
  output [31:0] Jout
);

  wire decoder_1_out0, decoder_1_out1, decoder_1_out2, decoder_1_out3, decoder_1_out4, decoder_1_out5,
       decoder_1_out6, decoder_1_out7;
  wire [31:0] Dout1, Dout2, Dout3, Dout4, Dout5, Dout6, Dout7, Dout8, SubMemoryLevel2_1_jout,
       SubMemoryLevel2_2_jout, SubMemoryLevel2_3_jout, SubMemoryLevel2_4_jout, SubMemoryLevel2_5_jout,
       SubMemoryLevel2_6_jout, SubMemoryLevel2_7_jout;

  Decoder #(.select(3)) decoder_1 (
    .out0(decoder_1_out0), .out1(decoder_1_out1), .out2(decoder_1_out2), .out3(decoder_1_out3),
    .out4(decoder_1_out4), .out5(decoder_1_out5), .out6(decoder_1_out6), .out7(decoder_1_out7),
    .sel(Addr[5:3]), .en(Wen));
  SubMemoryLevel2 SubMemoryLevel2_1 (
    .Jen(Jen), .Wen(decoder_1_out0), .Din(Din), .Jin(Jin), .Addr(Addr[2:0]), .clk(clk), .Dout(Dout1),
    .Jout(SubMemoryLevel2_1_jout));
  SubMemoryLevel2 SubMemoryLevel2_3 (
    .Jen(Jen), .Wen(decoder_1_out1), .Din(Din), .Jin(SubMemoryLevel2_1_jout), .Addr(Addr[2:0]), .clk(clk),
    .Dout(Dout2), .Jout(SubMemoryLevel2_3_jout));
  SubMemoryLevel2 SubMemoryLevel2_5 (
    .Jen(Jen), .Wen(decoder_1_out2), .Din(Din), .Jin(SubMemoryLevel2_3_jout), .Addr(Addr[2:0]), .clk(clk),
    .Dout(Dout3), .Jout(SubMemoryLevel2_5_jout));
  SubMemoryLevel2 SubMemoryLevel2_7 (
    .Jen(Jen), .Wen(decoder_1_out3), .Din(Din), .Jin(SubMemoryLevel2_5_jout), .Addr(Addr[2:0]), .clk(clk),
    .Dout(Dout4), .Jout(SubMemoryLevel2_7_jout));
  SubMemoryLevel2 SubMemoryLevel2_2 (
    .Jen(Jen), .Wen(decoder_1_out4), .Din(Din), .Jin(SubMemoryLevel2_7_jout), .Addr(Addr[2:0]), .clk(clk),
    .Dout(Dout5), .Jout(SubMemoryLevel2_2_jout));
  SubMemoryLevel2 SubMemoryLevel2_4 (
    .Jen(Jen), .Wen(decoder_1_out5), .Din(Din), .Jin(SubMemoryLevel2_2_jout), .Addr(Addr[2:0]), .clk(clk),
    .Dout(Dout6), .Jout(SubMemoryLevel2_4_jout));
  SubMemoryLevel2 SubMemoryLevel2_6 (
    .Jen(Jen), .Wen(decoder_1_out6), .Din(Din), .Jin(SubMemoryLevel2_4_jout), .Addr(Addr[2:0]), .clk(clk),
    .Dout(Dout7), .Jout(SubMemoryLevel2_6_jout));
  SubMemoryLevel2 SubMemoryLevel2_8 (
    .Jen(Jen), .Wen(decoder_1_out7), .Din(Din), .Jin(SubMemoryLevel2_6_jout), .Addr(Addr[2:0]), .clk(clk),
    .Dout(Dout8), .Jout(Jout));
  Multiplexer #(.select(3), .width(32)) multiplexer_1 (
    .in0(Dout1), .in1(Dout2), .in2(Dout3), .in3(Dout4), .in4(Dout5), .in5(Dout6), .in6(Dout7), .in7(Dout8),
    .out(Dout), .sel(Addr[5:3]));

  // Other names for the same wires on the sheet: Addr_t[2:0] = Addr[2:0]; AddrSelect[2:0] = Addr[5:3]
endmodule

module MipsMemory (
  input  Jen,
  input  Wen,
  input  [31:0] Din,
  input  [31:0] Jin,
  input  [8:0] Addr,
  input  clk,
  output [31:0] Dout,
  output [31:0] Jout
);

  wire decoder_1_out0, decoder_1_out1, decoder_1_out2, decoder_1_out3, decoder_1_out4, decoder_1_out5,
       decoder_1_out6, decoder_1_out7;
  wire [31:0] Dout1, Dout2, Dout3, Dout4, Dout5, Dout6, Dout7, Dout8, SubMemoryLevel1_1_jout,
       SubMemoryLevel1_2_jout, SubMemoryLevel1_3_jout, SubMemoryLevel1_4_jout, SubMemoryLevel1_5_jout,
       SubMemoryLevel1_6_jout, SubMemoryLevel1_7_jout;

  Decoder #(.select(3)) decoder_1 (
    .out0(decoder_1_out0), .out1(decoder_1_out1), .out2(decoder_1_out2), .out3(decoder_1_out3),
    .out4(decoder_1_out4), .out5(decoder_1_out5), .out6(decoder_1_out6), .out7(decoder_1_out7),
    .sel(Addr[8:6]), .en(Wen));
  SubMemoryLevel1 SubMemoryLevel1_1 (
    .Jen(Jen), .Wen(decoder_1_out0), .Din(Din), .Jin(Jin), .Addr(Addr[5:0]), .clk(clk), .Dout(Dout1),
    .Jout(SubMemoryLevel1_1_jout));
  SubMemoryLevel1 SubMemoryLevel1_3 (
    .Jen(Jen), .Wen(decoder_1_out1), .Din(Din), .Jin(SubMemoryLevel1_1_jout), .Addr(Addr[5:0]), .clk(clk),
    .Dout(Dout2), .Jout(SubMemoryLevel1_3_jout));
  SubMemoryLevel1 SubMemoryLevel1_5 (
    .Jen(Jen), .Wen(decoder_1_out2), .Din(Din), .Jin(SubMemoryLevel1_3_jout), .Addr(Addr[5:0]), .clk(clk),
    .Dout(Dout3), .Jout(SubMemoryLevel1_5_jout));
  SubMemoryLevel1 SubMemoryLevel1_7 (
    .Jen(Jen), .Wen(decoder_1_out3), .Din(Din), .Jin(SubMemoryLevel1_5_jout), .Addr(Addr[5:0]), .clk(clk),
    .Dout(Dout4), .Jout(SubMemoryLevel1_7_jout));
  SubMemoryLevel1 SubMemoryLevel1_2 (
    .Jen(Jen), .Wen(decoder_1_out4), .Din(Din), .Jin(SubMemoryLevel1_7_jout), .Addr(Addr[5:0]), .clk(clk),
    .Dout(Dout5), .Jout(SubMemoryLevel1_2_jout));
  SubMemoryLevel1 SubMemoryLevel1_4 (
    .Jen(Jen), .Wen(decoder_1_out5), .Din(Din), .Jin(SubMemoryLevel1_2_jout), .Addr(Addr[5:0]), .clk(clk),
    .Dout(Dout6), .Jout(SubMemoryLevel1_4_jout));
  SubMemoryLevel1 SubMemoryLevel1_6 (
    .Jen(Jen), .Wen(decoder_1_out6), .Din(Din), .Jin(SubMemoryLevel1_4_jout), .Addr(Addr[5:0]), .clk(clk),
    .Dout(Dout7), .Jout(SubMemoryLevel1_6_jout));
  SubMemoryLevel1 SubMemoryLevel1_8 (
    .Jen(Jen), .Wen(decoder_1_out7), .Din(Din), .Jin(SubMemoryLevel1_6_jout), .Addr(Addr[5:0]), .clk(clk),
    .Dout(Dout8), .Jout(Jout));
  Multiplexer #(.select(3), .width(32)) multiplexer_1 (
    .in0(Dout1), .in1(Dout2), .in2(Dout3), .in3(Dout4), .in4(Dout5), .in5(Dout6), .in6(Dout7), .in7(Dout8),
    .out(Dout), .sel(Addr[8:6]));

  // Other names for the same wires on the sheet: Addr_t[5:0] = Addr[5:0]; AddrSelect[2:0] = Addr[8:6]
endmodule

module IR_and_ID (
  input  [31:0] Instruction,
  input  Stall,
  input  clk,
  input  rst,
  output [31:0] InstructionOut,
  output [25:0] JumpAddress,
  output [5:0] funct,
  output [4:0] shamt,
  output [4:0] rd,
  output [4:0] rt,
  output [4:0] rs,
  output [5:0] opcode,
  output [31:0] SignExt_Imd
);

  wire not_1_out;

  Register #(.width(32)) Instruction_Register (
    .D(Instruction), .en(not_1_out), .clk(clk), .Q({InstructionOut[31:6], funct}), .clr(rst));
  not not_1 (not_1_out, Stall);
  assign SignExt_Imd = {{16{InstructionOut[15]}}, {InstructionOut[15:6], funct}};  // Bit_Extender bit_extender_1

  assign InstructionOut[5:0] = funct;
  assign JumpAddress = {InstructionOut[25:6], funct};
  assign opcode = InstructionOut[31:26];
  assign rd = InstructionOut[15:11];
  assign rs = InstructionOut[25:21];
  assign rt = InstructionOut[20:16];
  assign shamt = InstructionOut[10:6];
endmodule

module InstDoneCircuit (
  input  Stall3,
  input  clk,
  input  rst,
  output InstDone
);

  wire and_1_out, d_ff_1_q, d_ff_2_q, d_ff_3_q, d_ff_4_q, not_1_out, or_1_out;

  D_Flip_Flop d_ff_1 (.D(1'b1), .clk(clk), .Q(d_ff_1_q), .reset(rst));  // open: Qn, preset
  D_Flip_Flop d_ff_2 (.D(d_ff_1_q), .clk(clk), .Q(d_ff_2_q), .reset(rst));  // open: Qn, preset
  D_Flip_Flop d_ff_3 (.D(d_ff_2_q), .clk(clk), .Q(d_ff_3_q), .reset(rst));  // open: Qn, preset
  not not_1 (not_1_out, Stall3);
  and and_1 (and_1_out, d_ff_3_q, not_1_out);
  D_Flip_Flop d_ff_4 (.D(d_ff_3_q), .clk(clk), .Q(d_ff_4_q), .preset(and_1_out), .reset(or_1_out));  // open: Qn
  or or_1 (or_1_out, rst, Stall3);
  D_Flip_Flop d_ff_5 (.D(d_ff_4_q), .clk(clk), .Q(InstDone), .reset(rst));  // open: Qn, preset
endmodule
