// Logisim project Multiplier.circ as structural Verilog: 13 circuits, main circuit Multiplier32Bit
module helpAdder (
  input  [63:0] X,
  input  [63:0] Y,
  input  [63:0] Z,
  output [63:0] sum,
  output [63:0] carry
);

  wire [63:0] and_1_out, and_2_out, and_3_out, or_1_out, xor_1_out;

  assign and_1_out = X & Y;  // AND_Gate and_1, 64 bits wide
  assign and_2_out = Y & Z;  // AND_Gate and_2, 64 bits wide
  assign and_3_out = X & Z;  // AND_Gate and_3, 64 bits wide
  assign xor_1_out = X ^ Z;  // XOR_Gate xor_1, 64 bits wide
  assign or_1_out = and_1_out | and_2_out | and_3_out;  // OR_Gate or_1, 64 bits wide
  assign sum = xor_1_out ^ Y;  // XOR_Gate xor_2, 64 bits wide
  Real_64bit_Shifter real_64bit_shifter_1 (
    .A(or_1_out), .amount(6'b000001), .dir(1'b0), .Shift_Type(1'b0), .Shifted_A(carry));
endmodule

module Reverse (
  input  [63:0] A,
  output [63:0] Shifted_A
);


  assign Shifted_A = {A[0], A[1], A[2], A[3], A[4], A[5], A[6], A[7], A[8], A[9], A[10], A[11], A[12], A[13], A[14], A[15], A[16], A[17], A[18], A[19], A[20], A[21], A[22], A[23], A[24], A[25], A[26], A[27], A[28], A[29], A[30], A[31], A[32], A[33], A[34], A[35], A[36], A[37], A[38], A[39], A[40], A[41], A[42], A[43], A[44], A[45], A[46], A[47], A[48], A[49], A[50], A[51], A[52], A[53], A[54], A[55], A[56], A[57], A[58], A[59], A[60], A[61], A[62], A[63]};
endmodule

module Left_Shifter (
  input  [63:0] Data_in,
  input  [5:0] Shift_amount,
  input  Fill_Bit,
  output [63:0] Data_out
);

  wire [1:0] bit_extender_1_out;
  wire [3:0] bit_extender_2_out;
  wire [7:0] bit_extender_3_out;
  wire [15:0] bit_extender_4_out;
  wire [31:0] bit_extender_5_out;
  wire [63:0] multiplexer_1_out, multiplexer_2_out, multiplexer_3_out, multiplexer_4_out, multiplexer_5_out;

  assign bit_extender_1_out = {{1{Fill_Bit}}, Fill_Bit};  // Bit_Extender bit_extender_1
  assign bit_extender_2_out = {{3{Fill_Bit}}, Fill_Bit};  // Bit_Extender bit_extender_2
  assign bit_extender_3_out = {{7{Fill_Bit}}, Fill_Bit};  // Bit_Extender bit_extender_3
  assign bit_extender_4_out = {{15{Fill_Bit}}, Fill_Bit};  // Bit_Extender bit_extender_4
  assign bit_extender_5_out = {{31{Fill_Bit}}, Fill_Bit};  // Bit_Extender bit_extender_5
  Multiplexer #(.width(64)) multiplexer_1 (
    .in0(Data_in), .in1({Data_in[62:0], Fill_Bit}), .out(multiplexer_1_out), .sel(Shift_amount[0]));
  Multiplexer #(.width(64)) multiplexer_2 (
    .in0(multiplexer_1_out), .in1({Data_in[61:0], bit_extender_1_out}), .out(multiplexer_2_out),
    .sel(Shift_amount[1]));
  Multiplexer #(.width(64)) multiplexer_3 (
    .in0(multiplexer_2_out), .in1({Data_in[59:0], bit_extender_2_out}), .out(multiplexer_3_out),
    .sel(Shift_amount[2]));
  Multiplexer #(.width(64)) multiplexer_4 (
    .in0(multiplexer_3_out), .in1({Data_in[55:0], bit_extender_3_out}), .out(multiplexer_4_out),
    .sel(Shift_amount[3]));
  Multiplexer #(.width(64)) multiplexer_5 (
    .in0(multiplexer_4_out), .in1({Data_in[47:0], bit_extender_4_out}), .out(multiplexer_5_out),
    .sel(Shift_amount[4]));
  Multiplexer #(.width(64)) multiplexer_6 (
    .in0(multiplexer_5_out), .in1({Data_in[31:0], bit_extender_5_out}), .out(Data_out), .sel(Shift_amount[5]));
endmodule

module Real_64bit_Shifter (
  input  [63:0] A,
  input  [5:0] amount,
  input  dir,
  input  Shift_Type,
  output [63:0] Shifted_A
);

  wire and_1_out;
  wire [63:0] left_shifter_1_data_out, multiplexer_1_out, reverse_1_shifted_a, reverse_2_shifted_a;

  and and_1 (and_1_out, A[63], Shift_Type, dir);
  Reverse reverse_1 (.A(A), .Shifted_A(reverse_1_shifted_a));
  Multiplexer #(.width(64)) multiplexer_1 (.in0(A), .in1(reverse_1_shifted_a), .out(multiplexer_1_out), .sel(dir));
  Left_Shifter left_shifter_1 (
    .Data_in(multiplexer_1_out), .Shift_amount(amount), .Fill_Bit(and_1_out),
    .Data_out(left_shifter_1_data_out));
  Reverse reverse_2 (.A(left_shifter_1_data_out), .Shifted_A(reverse_2_shifted_a));
  Multiplexer #(.width(64)) multiplexer_2 (
    .in0(left_shifter_1_data_out), .in1(reverse_2_shifted_a), .out(Shifted_A), .sel(dir));
endmodule

module Multiplier32Bit (
  input  [31:0] a,
  input  [31:0] b,
  input  start,
  input  clk,
  input  rst_n,
  output done,
  output [31:0] res_lo,
  output [31:0] res_hi
);

  wire and_1_out, comparator_1_eq, d_ff_1_q, not_1_out, not_2_out, or_1_out, or_2_out, or_3_out;
  wire [1:0] Reg_B_q, Reg_carry_q_2, Reg_Sum_q_2;
  wire [3:0] counter_1_q;
  wire [27:0] Reg_carry_q, Reg_Sum_q;
  wire [29:0] Reg_B_q_2;
  wire [31:0] multiplexer_3_out, real_shifter_32bit_1_shifted_a;
  wire [33:0] csa_34bit_1_carry, csa_34bit_1_sum, mult_gen_1_a2_out, mult_gen_1_a3_out, mult_gen_1_a_out,
       multiplexer_4_out, Reg_carry_q_3, Reg_Sum_q_3;
  wire [63:0] adder_2_out, helpadder_1_carry, helpadder_1_sum, multiplexer_1_out, multiplexer_2_out;

  not not_1 (not_1_out, rst_n);
  or or_1 (or_1_out, start, d_ff_1_q);
  Multiplexer #(.width(64)) multiplexer_1 (
    .in0({64{1'b0}}), .in1({2'b00, a, {30{1'b0}}}), .out(multiplexer_1_out), .sel(b[30]));
  Multiplexer #(.width(64)) multiplexer_2 (
    .in0({64{1'b0}}), .in1({1'b0, a, {31{1'b0}}}), .out(multiplexer_2_out), .sel(b[31]));
  and and_1 (and_1_out, not_2_out, or_1_out);
  not not_2 (not_2_out, done);
  D_Flip_Flop d_ff_1 (.D(and_1_out), .clk(clk), .Q(d_ff_1_q));  // open: Qn, preset, reset
  or or_2 (or_2_out, not_1_out, start);
  Multiplexer #(.width(32)) multiplexer_3 (
    .in0(real_shifter_32bit_1_shifted_a), .in1({2'b00, b[29:0]}), .out(multiplexer_3_out), .sel(start));
  Counter #(.max('hf), .width(4)) counter_1 (
    .clr(or_2_out), .count(d_ff_1_q), .clk(clk), .Q(counter_1_q));  // open: load, up, D, carry
  or or_3 (or_3_out, start, d_ff_1_q);
  Register #(.width(32)) Reg_B (
    .D(multiplexer_3_out), .en(or_3_out), .clk(clk), .Q({Reg_B_q_2, Reg_B_q}));  // open: clr
  Register #(.width(64)) Reg_Sum (
    .D({2'b00, csa_34bit_1_sum, Reg_Sum_q}), .en(d_ff_1_q), .clk(clk),
    .Q({Reg_Sum_q_3, Reg_Sum_q, Reg_Sum_q_2}), .clr(start));
  Register #(.width(64)) Reg_carry (
    .D({2'b00, csa_34bit_1_carry, Reg_carry_q}), .en(d_ff_1_q), .clk(clk),
    .Q({Reg_carry_q_3, Reg_carry_q, Reg_carry_q_2}), .clr(start));
  Comparator #(.mode("unsigned"), .width(4)) comparator_1 (
    .a(counter_1_q), .b(4'b0010), .eq(comparator_1_eq));  // open: gt, lt
  Real_shifter_32bit real_shifter_32bit_1 (
    .A({Reg_B_q_2, Reg_B_q}), .amount(5'b00010), .dir(1'b1), .Shift_Type(1'b0),
    .Shifted_A(real_shifter_32bit_1_shifted_a));
  and and_2 (done, d_ff_1_q, comparator_1_eq);
  Mult_Gen mult_gen_1 (.A(a), .A_Out(mult_gen_1_a_out), .A2_Out(mult_gen_1_a2_out), .A3_Out(mult_gen_1_a3_out));
  Multiplexer #(.select(2), .width(34)) multiplexer_4 (
    .in0({34{1'b0}}), .in1(mult_gen_1_a_out), .in2(mult_gen_1_a2_out), .in3(mult_gen_1_a3_out),
    .out(multiplexer_4_out), .sel(Reg_B_q));
  helpAdder helpadder_1 (
    .X(multiplexer_1_out), .Y(multiplexer_2_out), .Z(adder_2_out), .sum(helpadder_1_sum),
    .carry(helpadder_1_carry));
  Adder #(.width(64)) adder_1 (.a(helpadder_1_sum), .b(helpadder_1_carry), .out({res_hi, res_lo}));  // open: cin, cout
  CSA_34bit csa_34bit_1 (
    .X(multiplexer_4_out), .Y(Reg_Sum_q_3), .Z(Reg_carry_q_3), .sum(csa_34bit_1_sum),
    .carry(csa_34bit_1_carry));
  Adder #(.width(64)) adder_2 (
    .a({Reg_Sum_q_3, Reg_Sum_q, Reg_Sum_q_2}), .b({Reg_carry_q_3, Reg_carry_q, Reg_carry_q_2}),
    .out(adder_2_out));  // open: cin, cout
endmodule

module Mult_Gen (
  input  [31:0] A,
  output [33:0] A_Out,
  output [33:0] A2_Out,
  output [33:0] A3_Out
);

  assign A_Out = {{2{1'b0}}, A};  // Bit_Extender bit_extender_1
  Real_34bit_shifter real_34bit_shifter_1 (
    .A(A_Out), .amount(6'b000001), .dir(1'b0), .Shift_Type(1'b0), .Shifted_A(A2_Out));
  Adder #(.width(34)) adder_1 (.a(A2_Out), .b(A_Out), .out(A3_Out));  // open: cin, cout
endmodule

module CSA_34bit (
  input  [33:0] X,
  input  [33:0] Y,
  input  [33:0] Z,
  output [33:0] sum,
  output [33:0] carry
);

  wire [33:0] and_1_out, and_2_out, and_3_out, or_1_out, xor_1_out;

  assign and_1_out = X & Y;  // AND_Gate and_1, 34 bits wide
  assign and_2_out = Y & Z;  // AND_Gate and_2, 34 bits wide
  assign and_3_out = X & Z;  // AND_Gate and_3, 34 bits wide
  assign xor_1_out = X ^ Z;  // XOR_Gate xor_1, 34 bits wide
  assign or_1_out = and_1_out | and_2_out | and_3_out;  // OR_Gate or_1, 34 bits wide
  assign sum = xor_1_out ^ Y;  // XOR_Gate xor_2, 34 bits wide
  Real_34bit_shifter real_34bit_shifter_1 (
    .A(or_1_out), .amount(6'b000001), .dir(1'b0), .Shift_Type(1'b0), .Shifted_A(carry));
endmodule

module Reverse_34bit (
  input  [33:0] A,
  output [33:0] Shifted_A
);


  assign Shifted_A = {A[0], A[1], A[2], A[3], A[4], A[5], A[6], A[7], A[8], A[9], A[10], A[11], A[12], A[13], A[14], A[15], A[16], A[17], A[18], A[19], A[20], A[21], A[22], A[23], A[24], A[25], A[26], A[27], A[28], A[29], A[30], A[31], A[32], A[33]};
endmodule

module Left_shifter_34bit (
  input  [33:0] Data_in,
  input  [5:0] Shift_amount,
  input  Fill_Bit,
  output [33:0] Data_out
);

  wire [1:0] bit_extender_1_out;
  wire [3:0] bit_extender_2_out;
  wire [7:0] bit_extender_3_out;
  wire [15:0] bit_extender_4_out;
  wire [31:0] bit_extender_5_out;
  wire [33:0] multiplexer_1_out, multiplexer_2_out, multiplexer_3_out, multiplexer_4_out, multiplexer_5_out;

  assign bit_extender_1_out = {{1{Fill_Bit}}, Fill_Bit};  // Bit_Extender bit_extender_1
  assign bit_extender_2_out = {{3{Fill_Bit}}, Fill_Bit};  // Bit_Extender bit_extender_2
  assign bit_extender_3_out = {{7{Fill_Bit}}, Fill_Bit};  // Bit_Extender bit_extender_3
  assign bit_extender_4_out = {{15{Fill_Bit}}, Fill_Bit};  // Bit_Extender bit_extender_4
  assign bit_extender_5_out = {{31{Fill_Bit}}, Fill_Bit};  // Bit_Extender bit_extender_5
  Multiplexer #(.width(34)) multiplexer_1 (
    .in0(Data_in), .in1({Data_in[32:0], Fill_Bit}), .out(multiplexer_1_out), .sel(Shift_amount[0]));
  Multiplexer #(.width(34)) multiplexer_2 (
    .in0(multiplexer_1_out), .in1({Data_in[31:0], bit_extender_1_out}), .out(multiplexer_2_out),
    .sel(Shift_amount[1]));
  Multiplexer #(.width(34)) multiplexer_3 (
    .in0(multiplexer_2_out), .in1({Data_in[29:0], bit_extender_2_out}), .out(multiplexer_3_out),
    .sel(Shift_amount[2]));
  Multiplexer #(.width(34)) multiplexer_4 (
    .in0(multiplexer_3_out), .in1({Data_in[25:0], bit_extender_3_out}), .out(multiplexer_4_out),
    .sel(Shift_amount[3]));
  Multiplexer #(.width(34)) multiplexer_5 (
    .in0(multiplexer_4_out), .in1({Data_in[17:0], bit_extender_4_out}), .out(multiplexer_5_out),
    .sel(Shift_amount[4]));
  Multiplexer #(.width(34)) multiplexer_6 (
    .in0(multiplexer_5_out), .in1({Data_in[1:0], bit_extender_5_out}), .out(Data_out), .sel(Shift_amount[5]));
endmodule

module Real_34bit_shifter (
  input  [33:0] A,
  input  [5:0] amount,
  input  dir,
  input  Shift_Type,
  output [33:0] Shifted_A
);

  wire and_1_out;
  wire [33:0] left_shifter_34bit_1_data_out, multiplexer_1_out, reverse_34bit_1_shifted_a,
       reverse_34bit_2_shifted_a;

  and and_1 (and_1_out, A[33], Shift_Type, dir);
  Reverse_34bit reverse_34bit_1 (.A(A), .Shifted_A(reverse_34bit_1_shifted_a));
  Multiplexer #(.width(34)) multiplexer_1 (
    .in0(A), .in1(reverse_34bit_1_shifted_a), .out(multiplexer_1_out), .sel(dir));
  Left_shifter_34bit left_shifter_34bit_1 (
    .Data_in(multiplexer_1_out), .Shift_amount(amount), .Fill_Bit(and_1_out),
    .Data_out(left_shifter_34bit_1_data_out));
  Reverse_34bit reverse_34bit_2 (.A(left_shifter_34bit_1_data_out), .Shifted_A(reverse_34bit_2_shifted_a));
  Multiplexer #(.width(34)) multiplexer_2 (
    .in0(left_shifter_34bit_1_data_out), .in1(reverse_34bit_2_shifted_a), .out(Shifted_A), .sel(dir));
endmodule

module Reverse_32bit (
  input  [31:0] A,
  output [31:0] Shifted_A
);


  assign Shifted_A = {A[0], A[1], A[2], A[3], A[4], A[5], A[6], A[7], A[8], A[9], A[10], A[11], A[12], A[13], A[14], A[15], A[16], A[17], A[18], A[19], A[20], A[21], A[22], A[23], A[24], A[25], A[26], A[27], A[28], A[29], A[30], A[31]};
endmodule

module Left_shifter_32bit (
  input  [31:0] Data_in,
  input  [4:0] Shift_amount,
  input  Fill_Bit,
  output [31:0] Data_out
);

  wire [1:0] bit_extender_1_out;
  wire [3:0] bit_extender_2_out;
  wire [7:0] bit_extender_3_out;
  wire [15:0] bit_extender_4_out;
  wire [31:0] multiplexer_1_out, multiplexer_2_out, multiplexer_3_out, multiplexer_4_out;

  assign bit_extender_1_out = {{1{Fill_Bit}}, Fill_Bit};  // Bit_Extender bit_extender_1
  assign bit_extender_2_out = {{3{Fill_Bit}}, Fill_Bit};  // Bit_Extender bit_extender_2
  assign bit_extender_3_out = {{7{Fill_Bit}}, Fill_Bit};  // Bit_Extender bit_extender_3
  assign bit_extender_4_out = {{15{Fill_Bit}}, Fill_Bit};  // Bit_Extender bit_extender_4
  Multiplexer #(.width(32)) multiplexer_1 (
    .in0(Data_in), .in1({Data_in[30:0], Fill_Bit}), .out(multiplexer_1_out), .sel(Shift_amount[0]));
  Multiplexer #(.width(32)) multiplexer_2 (
    .in0(multiplexer_1_out), .in1({Data_in[29:0], bit_extender_1_out}), .out(multiplexer_2_out),
    .sel(Shift_amount[1]));
  Multiplexer #(.width(32)) multiplexer_3 (
    .in0(multiplexer_2_out), .in1({Data_in[27:0], bit_extender_2_out}), .out(multiplexer_3_out),
    .sel(Shift_amount[2]));
  Multiplexer #(.width(32)) multiplexer_4 (
    .in0(multiplexer_3_out), .in1({Data_in[23:0], bit_extender_3_out}), .out(multiplexer_4_out),
    .sel(Shift_amount[3]));
  Multiplexer #(.width(32)) multiplexer_5 (
    .in0(multiplexer_4_out), .in1({Data_in[15:0], bit_extender_4_out}), .out(Data_out), .sel(Shift_amount[4]));
endmodule

module Real_shifter_32bit (
  input  [31:0] A,
  input  [4:0] amount,
  input  dir,
  input  Shift_Type,
  output [31:0] Shifted_A
);

  wire and_1_out;
  wire [31:0] left_shifter_32bit_1_data_out, multiplexer_1_out, reverse_32bit_1_shifted_a,
       reverse_32bit_2_shifted_a;

  and and_1 (and_1_out, A[31], Shift_Type, dir);
  Reverse_32bit reverse_32bit_1 (.A(A), .Shifted_A(reverse_32bit_1_shifted_a));
  Multiplexer #(.width(32)) multiplexer_1 (
    .in0(A), .in1(reverse_32bit_1_shifted_a), .out(multiplexer_1_out), .sel(dir));
  Left_shifter_32bit left_shifter_32bit_1 (
    .Data_in(multiplexer_1_out), .Shift_amount(amount), .Fill_Bit(and_1_out),
    .Data_out(left_shifter_32bit_1_data_out));
  Reverse_32bit reverse_32bit_2 (.A(left_shifter_32bit_1_data_out), .Shifted_A(reverse_32bit_2_shifted_a));
  Multiplexer #(.width(32)) multiplexer_2 (
    .in0(left_shifter_32bit_1_data_out), .in1(reverse_32bit_2_shifted_a), .out(Shifted_A), .sel(dir));
endmodule
